# Fritzing sketch rpi_apa102 (saved by Fritzing 0.9.3b)
breadboards: 1

parts:
  Raspberry_Pi = Raspberry Pi 2
  level_shifter_74HCT125 = IC, DIP package, 14 pins [chip_label=74HCT125]
  APA102_RGB_LED_Strip = APA102 RGB LED Strip
  5V_power_supply_for_LED_strip = Power plug

nets:
  GND: Raspberry_Pi.GND, level_shifter_74HCT125.pin1, level_shifter_74HCT125.pin4, level_shifter_74HCT125.pin7, APA102_RGB_LED_Strip.GND, 5V_power_supply_for_LED_strip.GND
  N1: Raspberry_Pi.GPIO24, level_shifter_74HCT125.pin5
  N2: Raspberry_Pi.GPIO23, level_shifter_74HCT125.pin2
  N3: level_shifter_74HCT125.pin3, APA102_RGB_LED_Strip.CI
  N4: level_shifter_74HCT125.pin6, APA102_RGB_LED_Strip.DI
  +5V: level_shifter_74HCT125.pin14, APA102_RGB_LED_Strip.+5V, 5V_power_supply_for_LED_strip.VCC

notes:
  5V Power supply for LED strip
  CLK: GPIO23
  DI: GPIO24

custom parts:
  APA102 RGB LED Strip: Digitally addressable RGB LED strip
